# Fritzing sketch ad8232 (saved by Fritzing 0.9.3b)
breadboards: 1

parts:
  Raspberry_Pi_3 = Raspberry Pi 3 [part_number=RPI-3-V1.2]
  IC1 = AD8232 HeartRate Monitor [part_number=SEN-12650 chip_label=IC package="DIP (Dual Inline) [THT]"]

nets:
  N1: Raspberry_Pi_3.GPIO17, IC1.LO-
  N2: Raspberry_Pi_3.GPIO23, IC1.OUTPUT
  N3: Raspberry_Pi_3.GPIO15, IC1.LO+
  GND: Raspberry_Pi_3.GND, IC1.GND
  5V: Raspberry_Pi_3.5V, IC1.3.3v

custom parts:
  AD8232 HeartRate Monitor: A DIP stand-in part for whatever IC you want. With 10 pins on a 600mil dual inline package (DIP) footprint.
